// Logisim project Processor.circ as structural Verilog: 13 circuits, main circuit SR_FF
module SR_FF (
  input  in_1,
  input  in_2,
  input  in_3,
  output out_4,
  output out_5
);

  wire nand_1_out, nand_2_out;

  nand nand_1 (nand_1_out, in_1, in_2);
  nand nand_2 (nand_2_out, in_2, in_3);
  nand nand_3 (out_4, nand_1_out, out_5);
  nand nand_4 (out_5, out_4, nand_2_out);
endmodule

module Board (
  input  in_1,
  input  in_2,
  input  in_3,
  input  in_4,
  input  in_5,
  input  in_6,
  input  in_7,
  input  in_8,
  input  in_9,
  input  [7:0] in_10,
  output [7:0] out_11
);

  RAM ram_1 (
    .addr({in_8, in_7, in_6, in_5, in_4, in_3, in_2, in_1}), .we(in_9), .oe(in_3), .clk(in_3), .din(in_10),
    .dout(out_11));
endmodule

module D_FF_level_triggered (
  input  in_1,
  input  CLK,
  output out_3,
  output out_4
);

  wire nand_1_out, nand_2_out, not_1_out;

  not not_1 (not_1_out, in_1);
  nand nand_1 (nand_1_out, in_1, CLK);
  nand nand_2 (nand_2_out, CLK, not_1_out);
  nand nand_3 (out_3, nand_1_out, out_4);
  nand nand_4 (out_4, out_3, nand_2_out);
endmodule

module PIPO_Register (
  input  in_1,
  input  in_2,
  input  in_3,
  input  in_4,
  input  LD,
  output out_6,
  output out_7,
  output out_8,
  output out_9
);

  wire d_ff_edge_triggered_1_out_4, d_ff_edge_triggered_2_out_4, d_ff_edge_triggered_3_out_4,
       d_ff_edge_triggered_4_out_4;

  D_FF_edge_triggered d_ff_edge_triggered_1 (
    .in_1(in_1), .in_2(LD), .out_3(out_6), .out_4(d_ff_edge_triggered_1_out_4));
  LED led_1 (.in(d_ff_edge_triggered_1_out_4));
  D_FF_edge_triggered d_ff_edge_triggered_2 (
    .in_1(in_2), .in_2(LD), .out_3(out_7), .out_4(d_ff_edge_triggered_2_out_4));
  LED led_2 (.in(d_ff_edge_triggered_2_out_4));
  D_FF_edge_triggered d_ff_edge_triggered_3 (
    .in_1(in_3), .in_2(LD), .out_3(out_8), .out_4(d_ff_edge_triggered_3_out_4));
  LED led_3 (.in(d_ff_edge_triggered_3_out_4));
  D_FF_edge_triggered d_ff_edge_triggered_4 (
    .in_1(in_4), .in_2(LD), .out_3(out_9), .out_4(d_ff_edge_triggered_4_out_4));
  LED led_4 (.in(d_ff_edge_triggered_4_out_4));
endmodule

module Accumulator (
  input  [3:0] in_1,
  input  LD,
  output [3:0] out_3
);

  PIPO_Register pipo_register_1 (
    .in_1(in_1[0]), .in_2(in_1[1]), .in_3(in_1[2]), .in_4(in_1[3]), .LD(LD), .out_6(out_3[0]),
    .out_7(out_3[1]), .out_8(out_3[2]), .out_9(out_3[3]));
endmodule

module Full_Adder (
  input  in_1,
  input  in_2,
  input  Cin,
  output Sum,
  output Cout
);

  wire and_1_out, and_2_out, xor_1_out;

  xor xor_1 (xor_1_out, in_1, in_2);
  and and_1 (and_1_out, xor_1_out, Cin);
  xor xor_2 (Sum, xor_1_out, Cin);
  and and_2 (and_2_out, in_2, in_1);
  or or_1 (Cout, and_1_out, and_2_out);
endmodule

module ALU (
  input  [3:0] Acc,
  input  [3:0] D_Reg,
  input  S0,
  input  S1,
  input  S2,
  input  Ir,
  input  Il,
  output Cout,
  output [3:0] ResultToAcc,
  output EN
);

  wire [3:0] and_1_out, fourbit_adder_subtractor_1_s0, multiplexer_1_out, not_1_out, or_1_out,
       shift_unit_1_s0, xor_1_out;

  assign not_1_out = ~Acc;  // NOT_Gate not_1, 4 bits wide
  assign and_1_out = Acc & D_Reg;  // AND_Gate and_1, 4 bits wide
  assign or_1_out = Acc | D_Reg;  // OR_Gate or_1, 4 bits wide
  assign xor_1_out = Acc ^ D_Reg;  // XOR_Gate xor_1, 4 bits wide
  FourBit_Adder_Subtractor fourbit_adder_subtractor_1 (
    .A0(Acc[0]), .A1(Acc[1]), .A2(Acc[2]), .A3(Acc[3]), .B0(D_Reg[0]), .B1(D_Reg[1]), .B2(D_Reg[2]),
    .B3(D_Reg[3]), .sub_mode(S0), .S0(fourbit_adder_subtractor_1_s0[0]),
    .S1(fourbit_adder_subtractor_1_s0[1]), .S2(fourbit_adder_subtractor_1_s0[2]),
    .S3(fourbit_adder_subtractor_1_s0[3]), .Cout(Cout));
  Shift_Unit shift_unit_1 (
    .Ir(Ir), .A0(Acc[0]), .A1(Acc[1]), .A2(Acc[2]), .A3(Acc[3]), .Il(Il), .right_shift(S0),
    .S0(shift_unit_1_s0[0]), .S1(shift_unit_1_s0[1]), .S2(shift_unit_1_s0[2]), .S3(shift_unit_1_s0[3]));
  Multiplexer #(.select(3), .width(4)) multiplexer_1 (
    .in0(fourbit_adder_subtractor_1_s0), .in1(fourbit_adder_subtractor_1_s0), .in2(not_1_out),
    .in3(and_1_out), .in4(or_1_out), .in5(xor_1_out), .in6(shift_unit_1_s0), .in7(shift_unit_1_s0),
    .out(multiplexer_1_out), .sel({S2, S1, S0}));
  Multiplexer #(.width(4)) multiplexer_2 (.in0(Acc), .in1(multiplexer_1_out), .out(ResultToAcc), .sel(EN));
endmodule

module FourBit_Adder_Subtractor (
  input  A0,
  input  A1,
  input  A2,
  input  A3,
  input  B0,
  input  B1,
  input  B2,
  input  B3,
  input  sub_mode,
  output S0,
  output S1,
  output S2,
  output S3,
  output Cout
);

  wire full_adder_1_cout, full_adder_2_cout, full_adder_3_cout, xor_1_out, xor_2_out, xor_3_out, xor_4_out;

  xor xor_1 (xor_1_out, sub_mode, B0);
  xor xor_2 (xor_2_out, sub_mode, B1);
  xor xor_3 (xor_3_out, sub_mode, B2);
  xor xor_4 (xor_4_out, sub_mode, B3);
  Full_Adder full_adder_1 (.in_1(A0), .in_2(xor_1_out), .Cin(sub_mode), .Sum(S0), .Cout(full_adder_1_cout));
  Full_Adder full_adder_2 (.in_1(A1), .in_2(xor_2_out), .Cin(full_adder_1_cout), .Sum(S1), .Cout(full_adder_2_cout));
  Full_Adder full_adder_3 (.in_1(A2), .in_2(xor_3_out), .Cin(full_adder_2_cout), .Sum(S2), .Cout(full_adder_3_cout));
  Full_Adder full_adder_4 (.in_1(A3), .in_2(xor_4_out), .Cin(full_adder_3_cout), .Sum(S3), .Cout(Cout));
endmodule

module D_FF_edge_triggered (
  input  in_1,
  input  in_2,
  output out_3,
  output out_4
);

  D_Flip_Flop d_ff_1 (.D(in_1), .clk(in_2), .Q(out_3), .Qn(out_4));  // open: preset, reset
endmodule

module Shift_Unit (
  input  Ir,
  input  A0,
  input  A1,
  input  A2,
  input  A3,
  input  Il,
  input  right_shift,
  output S0,
  output S1,
  output S2,
  output S3
);

  Multiplexer multiplexer_1 (.in0(Ir), .in1(A1), .out(S0), .sel(right_shift));
  Multiplexer multiplexer_2 (.in0(A0), .in1(A2), .out(S1), .sel(right_shift));
  Multiplexer multiplexer_3 (.in0(A1), .in1(A3), .out(S2), .sel(right_shift));
  Multiplexer multiplexer_4 (.in0(A2), .in1(Il), .out(S3), .sel(right_shift));
endmodule

module SystemBus (
  input  [3:0] ADDBUS_L,
  input  [3:0] ADDBUS_H,
  input  in_3,
  input  in_4,
  input  in_5,
  output out_6,
  output [3:0] DataBus
);

  wire alu_1_en, and_1_out, button_1_out, button_2_out, decoder_1_out0, decoder_1_out3, decoder_1_out5,
       decoder_1_out8, decoder_1_out9, decoder_1_out10, decoder_1_out11, decoder_1_out12, decoder_1_out13,
       decoder_1_out14, decoder_1_out15, decoder_2_out0, decoder_2_out1, decoder_2_out2, decoder_2_out3,
       decoder_3_out0, decoder_3_out1, decoder_3_out2, decoder_3_out4, decoder_3_out5, decoder_3_out6,
       not_1_out, or_1_out, or_2_out, or_3_out, or_4_out, or_5_out, or_6_out, or_7_out, synccounter_2_out_7;
  wire [2:0] IR_out_3_2, multiplexer_3_out, synccounter_2_out_4;
  wire [3:0] ACC_out_3, alu_1_resulttoacc, BR_out_3, CR_out_3, DR_out_3, multiplexer_2_out,
       multiplexer_4_out, multiplexer_5_out, ram_1_dout, synccounter_1_out_4;
  wire [3:3] IR_out_3;
  wire [7:0] multiplexer_1_out;

  Button button_1 (.out(button_1_out));
  SyncCounter synccounter_1 (
    .EN(in_3), .CLK(decoder_3_out1), .RST(button_1_out), .out_4(synccounter_1_out_4[0]),
    .out_5(synccounter_1_out_4[1]), .out_6(synccounter_1_out_4[2]), .out_7(synccounter_1_out_4[3]));
  Button button_2 (.out(button_2_out));
  Hex_Digit_Display hex_digit_display_1 (.value(synccounter_1_out_4));  // open: dp
  or or_1 (or_1_out, in_5, and_1_out);
  Multiplexer #(.width(8)) multiplexer_1 (
    .in0({ADDBUS_H, ADDBUS_L}), .in1({4'b0000, synccounter_1_out_4}), .out(multiplexer_1_out), .sel(or_7_out));
  ALU alu_1 (
    .Acc(ACC_out_3), .D_Reg(DR_out_3), .S0(IR_out_3_2[0]), .S1(IR_out_3_2[1]), .S2(IR_out_3_2[2]), .Ir(1'b0),
    .Il(1'b0), .Cout(out_6), .ResultToAcc(alu_1_resulttoacc), .EN(alu_1_en));
  Decoder #(.select(4)) decoder_1 (
    .out0(decoder_1_out0), .out3(decoder_1_out3), .out5(decoder_1_out5), .out8(decoder_1_out8),
    .out9(decoder_1_out9), .out10(decoder_1_out10), .out11(decoder_1_out11), .out12(decoder_1_out12),
    .out13(decoder_1_out13), .out14(decoder_1_out14), .out15(decoder_1_out15),
    .sel({IR_out_3[3], IR_out_3_2}), .en(alu_1_en));  // open: out1, out2, out4, out6, out7
  Decoder #(.select(2)) decoder_2 (
    .out0(decoder_2_out0), .out1(decoder_2_out1), .out2(decoder_2_out2), .out3(decoder_2_out3),
    .sel(ADDBUS_L[1:0]), .en(decoder_1_out0));
  SyncCounter synccounter_2 (
    .EN(in_4), .CLK(button_2_out), .RST(or_1_out), .out_4(synccounter_2_out_4[0]),
    .out_5(synccounter_2_out_4[1]), .out_6(synccounter_2_out_4[2]), .out_7(synccounter_2_out_7));
  Hex_Digit_Display hex_digit_display_2 (.value(multiplexer_2_out));  // open: dp
  Multiplexer #(.width(4)) multiplexer_2 (
    .in0(alu_1_resulttoacc), .in1(DataBus), .out(multiplexer_2_out), .sel(decoder_1_out0));
  or or_2 (or_2_out, decoder_1_out11, decoder_3_out1, decoder_1_out13);
  or or_3 (or_3_out, decoder_1_out3, decoder_1_out5, decoder_1_out8, decoder_1_out9, decoder_1_out10, decoder_1_out12, decoder_1_out14, decoder_1_out15);
  or or_4 (or_4_out, decoder_2_out2, decoder_1_out13);
  not not_1 (not_1_out, IR_out_3[3]);
  Decoder #(.enable("false"), .select(3)) decoder_3 (
    .out0(decoder_3_out0), .out1(decoder_3_out1), .out2(decoder_3_out2), .out3(alu_1_en),
    .out4(decoder_3_out4), .out5(decoder_3_out5), .out6(decoder_3_out6), .sel(synccounter_2_out_4));  // open: out7
  or or_5 (or_5_out, decoder_2_out3, or_3_out);
  RAM #(.dataWidth(4)) ram_1 (
    .addr(multiplexer_1_out), .we(decoder_1_out11), .oe(or_6_out), .clk(or_2_out), .din(DataBus),
    .dout(ram_1_dout));
  or or_6 (or_6_out, decoder_1_out13, decoder_3_out1);
  and and_1 (and_1_out, decoder_3_out4, or_3_out);
  Accumulator IR (.in_1(DataBus), .LD(decoder_3_out2), .out_3({IR_out_3[3], IR_out_3_2}));
  Accumulator BR (.in_1(DataBus), .LD(decoder_2_out0), .out_3(BR_out_3));
  Accumulator CR (.in_1(DataBus), .LD(decoder_2_out1), .out_3(CR_out_3));
  Accumulator DR (.in_1(DataBus), .LD(or_4_out), .out_3(DR_out_3));
  Accumulator ACC (.in_1(multiplexer_2_out), .LD(or_5_out), .out_3(ACC_out_3));
  Hex_Digit_Display hex_digit_display_3 (.value({IR_out_3[3], IR_out_3_2}));  // open: dp
  or or_7 (or_7_out, decoder_3_out0, decoder_3_out1);
  Hex_Digit_Display hex_digit_display_4 (.value(ACC_out_3));  // open: dp
  Hex_Digit_Display hex_digit_display_5 (.value(DR_out_3));  // open: dp
  Multiplexer #(.width(3)) multiplexer_3 (
    .in0(IR_out_3_2), .in1({1'b0, ADDBUS_L[3:2]}), .out(multiplexer_3_out), .sel(not_1_out));
  Hex_Digit_Display hex_digit_display_6 (.value(CR_out_3));  // open: dp
  Multiplexer #(.width(4)) multiplexer_4 (.in0(4'b0000), .in1(ram_1_dout), .out(multiplexer_4_out), .sel(or_2_out));
  Hex_Digit_Display hex_digit_display_7 (.value(BR_out_3));  // open: dp
  Multiplexer #(.select(3), .width(4)) multiplexer_5 (
    .in0(ACC_out_3), .in1(BR_out_3), .in2(CR_out_3), .in3(DR_out_3), .in4({IR_out_3[3], IR_out_3_2}),
    .in5(multiplexer_4_out), .out(multiplexer_5_out), .sel(multiplexer_3_out));  // open: in6, in7
  Multiplexer #(.width(4)) multiplexer_6 (
    .in0(multiplexer_5_out), .in1(multiplexer_4_out), .out(DataBus), .sel(or_7_out));
  Hex_Digit_Display hex_digit_display_8 (.value(DataBus));  // open: dp
  // also tied to GND on the sheet: synccounter_2_out_7
endmodule

module SyncCounter (
  input  EN,
  input  CLK,
  input  RST,
  output out_4,
  output out_5,
  output out_6,
  output out_7
);

  wire and_1_out, and_2_out;

  J_K_Flip_Flop j_k_ff_1 (.J(EN), .K(EN), .clk(CLK), .Q(out_4), .reset(RST));  // open: Qn, preset
  J_K_Flip_Flop j_k_ff_2 (.J(out_4), .K(out_4), .clk(CLK), .Q(out_5), .reset(RST));  // open: Qn, preset
  and and_1 (and_1_out, out_4, out_5);
  J_K_Flip_Flop j_k_ff_3 (.J(and_1_out), .K(and_1_out), .clk(CLK), .Q(out_6), .reset(RST));  // open: Qn, preset
  and and_2 (and_2_out, and_1_out, out_6);
  J_K_Flip_Flop j_k_ff_4 (.J(and_2_out), .K(and_2_out), .clk(CLK), .Q(out_7), .reset(RST));  // open: Qn, preset
endmodule

module ControlUnit (
  input  in_1,
  input  in_2,
  input  in_3
);

  wire and_1_out, button_1_out, button_2_out, decoder_1_out0, decoder_1_out1, decoder_1_out2, decoder_1_out3,
       decoder_1_out4, decoder_1_out5, decoder_1_out6, or_1_out, or_2_out, synccounter_2_out_7, undriven;
  wire [2:0] synccounter_2_out_4;
  wire [3:0] synccounter_1_out_4;

  Button button_1 (.out(button_1_out));
  SyncCounter synccounter_1 (
    .EN(in_1), .CLK(decoder_1_out1), .RST(button_1_out), .out_4(synccounter_1_out_4[0]),
    .out_5(synccounter_1_out_4[1]), .out_6(synccounter_1_out_4[2]), .out_7(synccounter_1_out_4[3]));
  Hex_Digit_Display hex_digit_display_1 (.value(synccounter_1_out_4));  // open: dp
  Button button_2 (.out(button_2_out));
  or or_1 (or_1_out, in_3, and_1_out);
  SyncCounter synccounter_2 (
    .EN(in_2), .CLK(button_2_out), .RST(or_1_out), .out_4(synccounter_2_out_4[0]),
    .out_5(synccounter_2_out_4[1]), .out_6(synccounter_2_out_4[2]), .out_7(synccounter_2_out_7));
  Decoder #(.enable("false"), .select(3)) decoder_1 (
    .out0(decoder_1_out0), .out1(decoder_1_out1), .out2(decoder_1_out2), .out3(decoder_1_out3),
    .out4(decoder_1_out4), .out5(decoder_1_out5), .out6(decoder_1_out6), .sel(synccounter_2_out_4));  // open: out7
  and and_1 (and_1_out, decoder_1_out4, undriven);
  or or_2 (or_2_out, decoder_1_out0, decoder_1_out1);
  // also tied to GND on the sheet: synccounter_2_out_7
endmodule
